// Logisim project ALU.circ as structural Verilog
// ALU 1Bit
module ALU_1_bit (
  input  A,
  input  B,
  input  Cin,
  input  Cin_2,
  input  [2:0] in_5,
  output Cout,
  output Cout_2,
  output out_8
);

  wire and_1_out, full_adder_1_bit_1_s, nand_1_out, nor_1_out, not_1_out, or_1_out, soustractor_1_s,
       xnor_1_out;

  FULL_ADDER_1_Bit full_adder_1_bit_1 (.A(A), .B(B), .C_i(Cin), .S(full_adder_1_bit_1_s), .C_o(Cout));
  or or_1 (or_1_out, A, B);
  and and_1 (and_1_out, A, B);
  not not_1 (not_1_out, B);
  Soustractor soustractor_1 (.A(A), .B(B), .Cin(Cin_2), .S(soustractor_1_s), .Cout(Cout_2));
  Pull_Resistor pull_resistor_1 (.node(Cout_2));
  nor nor_1 (nor_1_out, A, B);
  nand nand_1 (nand_1_out, A, B);
  xnor xnor_1 (xnor_1_out, A, B);
  MUX_8__1_1Bit mux_8_1_1bit_1 (
    .in_1(full_adder_1_bit_1_s), .in_2(or_1_out), .in_3(and_1_out), .in_4(not_1_out), .in_5(soustractor_1_s),
    .in_6(nor_1_out), .in_7(nand_1_out), .in_8(xnor_1_out), .out_10(out_8), .in_9(in_5));
endmodule

// ALU
module ALU_PROC (
  input  [3:0] in_1,
  input  [3:0] in_2,
  input  Ci,
  input  [2:0] S,
  output Co,
  output [3:0] out_6
);

  wire alu_1_bit_1_cout, alu_1_bit_1_cout_2, alu_1_bit_2_cout, alu_1_bit_2_cout_2, alu_1_bit_3_cout,
       alu_1_bit_3_cout_2, alu_1_bit_4_cout;

  ALU_1_bit alu_1_bit_1 (
    .A(in_1[0]), .B(in_2[0]), .out_8(out_6[0]), .in_5(S), .Cin(Ci), .Cout(alu_1_bit_1_cout),
    .Cout_2(alu_1_bit_1_cout_2), .Cin_2(Ci));
  ALU_1_bit alu_1_bit_2 (
    .A(in_1[1]), .B(in_2[1]), .out_8(out_6[1]), .in_5(S), .Cin(alu_1_bit_1_cout), .Cout(alu_1_bit_2_cout),
    .Cout_2(alu_1_bit_2_cout_2), .Cin_2(alu_1_bit_1_cout_2));
  ALU_1_bit alu_1_bit_3 (
    .A(in_1[2]), .B(in_2[2]), .out_8(out_6[2]), .in_5(S), .Cin(alu_1_bit_2_cout), .Cout(alu_1_bit_3_cout),
    .Cout_2(alu_1_bit_3_cout_2), .Cin_2(alu_1_bit_2_cout_2));
  ALU_1_bit alu_1_bit_4 (
    .A(in_1[3]), .B(in_2[3]), .out_8(out_6[3]), .in_5(S), .Cin(alu_1_bit_3_cout), .Cout(alu_1_bit_4_cout),
    .Cout_2(alu_1_bit_4_cout), .Cin_2(alu_1_bit_3_cout_2));
  buf buffer_1 (Co, alu_1_bit_4_cout);
endmodule

// MUX 4BIT
module MUX_8__1_4BIT (
  input  [3:0] in_1,
  input  [3:0] in_2,
  input  [3:0] in_3,
  input  [3:0] in_4,
  input  [3:0] in_5,
  input  [3:0] in_6,
  input  [3:0] in_7,
  input  [3:0] in_8,
  input  [2:0] in_9,
  output [3:0] out_10
);

  MUX_8__1_1Bit mux_8_1_1bit_1 (
    .in_1(in_1[0]), .in_2(in_2[0]), .in_3(in_3[0]), .in_4(in_4[0]), .in_5(in_5[0]), .in_6(in_6[0]),
    .in_7(in_7[0]), .in_8(in_8[0]), .out_10(out_10[0]), .in_9(in_9));
  MUX_8__1_1Bit mux_8_1_1bit_2 (
    .in_1(in_1[1]), .in_2(in_2[1]), .in_3(in_3[1]), .in_4(in_4[1]), .in_5(in_5[1]), .in_6(in_6[1]),
    .in_7(in_7[1]), .in_8(in_8[1]), .out_10(out_10[1]), .in_9(in_9));
  MUX_8__1_1Bit mux_8_1_1bit_3 (
    .in_1(in_1[2]), .in_2(in_2[2]), .in_3(in_3[2]), .in_4(in_4[2]), .in_5(in_5[2]), .in_6(in_6[2]),
    .in_7(in_7[2]), .in_8(in_8[2]), .out_10(out_10[2]), .in_9(in_9));
  MUX_8__1_1Bit mux_8_1_1bit_4 (
    .in_1(in_1[3]), .in_2(in_2[3]), .in_3(in_3[3]), .in_4(in_4[3]), .in_5(in_5[3]), .in_6(in_6[3]),
    .in_7(in_7[3]), .in_8(in_8[3]), .out_10(out_10[3]), .in_9(in_9));
endmodule

module Soustractor (
  input  A,
  input  B,
  input  Cin,
  output S,
  output Cout
);

  wire and_1_out, and_2_out, and_3_out, and_4_out, and_5_out, and_6_out, and_7_out, not_1_out, not_2_out,
       not_3_out, not_4_out, not_5_out, not_6_out, not_7_out, not_8_out;

  not not_1 (not_1_out, A);
  not not_2 (not_2_out, B);
  not not_3 (not_3_out, A);
  not not_4 (not_4_out, Cin);
  not not_5 (not_5_out, B);
  not not_6 (not_6_out, Cin);
  not not_7 (not_7_out, A);
  not not_8 (not_8_out, A);
  and and_1 (and_1_out, not_1_out, not_2_out, Cin);
  and and_2 (and_2_out, not_3_out, B, not_4_out);
  and and_3 (and_3_out, A, not_5_out, not_6_out);
  and and_4 (and_4_out, A, B, Cin);
  and and_5 (and_5_out, not_7_out, Cin);
  and and_6 (and_6_out, not_8_out, B);
  and and_7 (and_7_out, B, Cin);
  or or_1 (S, and_1_out, and_2_out, and_3_out, and_4_out);
  or or_2 (Cout, and_5_out, and_6_out, and_7_out);
endmodule
