// Logisim project CPU.circ as structural Verilog: 5 circuits, main circuit main
// Adress Unit
module main (
);

  wire au_1_wad_2, button_1_out, clock_1_out, uc_1_source_sel, uc_1_wad, uc_1_wpc, uc_1_write;
  wire [1:0] uc_1_rwrite_sel;
  wire [2:0] uc_1_alu_sel;
  wire [3:0] alu_proc_1_out_6, au_1_mad_2, au_1_pc_out, au_1_pc_out_2, multiplexer_1_out, ram_1_data,
       regfile_1_xout, regfile_1_yout, uc_1_mad, uc_1_pcout, uc_1_rx_sel, uc_1_ry_sel;
  wire [11:0] rom_1_data;

  // Probe on au_1_pc_out_2
  ROM #(.addrWidth(4), .dataWidth(12)) rom_1 (.addr(au_1_pc_out_2), .data(rom_1_data), .sel(1'b1));
  // Probe on ram_1_data
  // Probe on rom_1_data
  Button button_1 (.out(button_1_out));
  // Probe on multiplexer_1_out
  Multiplexer #(.width(4), .enable("false")) multiplexer_1 (
    .in0(alu_proc_1_out_6), .in1(ram_1_data), .out(multiplexer_1_out), .sel(uc_1_source_sel));
  // Probe on uc_1_rwrite_sel
  // Probe on uc_1_pcout
  // Probe on au_1_wad_2
  // Probe on uc_1_write
  UC uc_1 (
    .In_in(rom_1_data), .Write(uc_1_write), .Source_Sel(uc_1_source_sel), .RWrite_Sel(uc_1_rwrite_sel),
    .RX_Sel(uc_1_rx_sel), .RY_Sel(uc_1_ry_sel), .ALU_Sel(uc_1_alu_sel), .wAD(uc_1_wad), .mAD(uc_1_mad),
    .wPC(uc_1_wpc), .PCin(au_1_pc_out), .PCout(uc_1_pcout), .RESET(button_1_out));  // open: Fetch
  // Probe on au_1_pc_out
  // Probe on au_1_mad_2
  RegFile regfile_1 (
    .XOut(regfile_1_xout), .YOut(regfile_1_yout), .Din(multiplexer_1_out), .RegSel(uc_1_rwrite_sel),
    .Write(uc_1_write), .Xsel(uc_1_rx_sel), .Ysel(uc_1_ry_sel));
  // Probe on uc_1_rx_sel
  // Probe on uc_1_ry_sel
  AU au_1 (
    .PC_Out(au_1_pc_out), .PC_in(uc_1_pcout), .PC_out_2(au_1_pc_out_2), .wPC(uc_1_wpc), .wAD(uc_1_wad),
    .wAD_2(au_1_wad_2), .mAD(uc_1_mad), .mAD_2(au_1_mad_2));
  Clock clock_1 (.out(clock_1_out));
  // Probe on uc_1_alu_sel
  RAM #(.addrWidth(4), .dataWidth(4), .bus("separate")) ram_1 (
    .addr(au_1_mad_2), .din(alu_proc_1_out_6), .data(ram_1_data), .str(au_1_wad_2), .clk(clock_1_out),
    .ld(1'b1));  // open: sel, clr
  // Probe on regfile_1_xout
  // Probe on alu_proc_1_out_6
  // Probe on regfile_1_yout
  ALU_PROC alu_proc_1 (
    .Ci(1'b0), .S(uc_1_alu_sel), .in_1(regfile_1_xout), .in_2(regfile_1_yout), .out_6(alu_proc_1_out_6));  // open: Co

  // Notes on the sheet:
  //   contents of rom_1 (hex, n*v repeats v):
  //   400 444 84 888
endmodule

module PC (
  input  [3:0] in,
  output [3:0] out
);

  REGISTER_4_bits register_4_bits_1 (.READ(1'b1), .D(in), .out_4(out), .Write(1'b1));
endmodule

module Test (
  input  [3:0] in_1
);

  wire button_1_out;
  wire [3:0] pc_increase_1_out, register_4_bits_1_out_4;

  // Probe on register_4_bits_1_out_4
  Button button_1 (.out(button_1_out));
  PC_Increase pc_increase_1 (.in(register_4_bits_1_out_4), .RESET(button_1_out), .out(pc_increase_1_out));
  // Probe on pc_increase_1_out
  // Probe on register_4_bits_1_out_4
  REGISTER_4_bits register_4_bits_1 (.READ(1'b1), .D(pc_increase_1_out), .out_4(register_4_bits_1_out_4), .Write(1'b1));
endmodule

module AD (
  input  [3:0] in,
  output [3:0] out
);

  REGISTER_4_bits register_4_bits_1 (.READ(1'b1), .D(in), .out_4(out), .Write(1'b1));
endmodule

// AdressUnit
module AU (
  input  wPC,
  input  [3:0] PC_in,
  input  wAD,
  input  [3:0] mAD,
  output [3:0] PC_out_2,
  output [3:0] PC_Out,
  output wAD_2,
  output [3:0] mAD_2
);

  PC pc_1 (.in(PC_in), .out(PC_Out));

  assign mAD_2 = mAD;
  assign PC_out_2 = PC_Out;
  assign wAD_2 = wAD;
endmodule
