// Logisim project CU.circ as structural Verilog
module UC (
  input  [11:0] In_in,
  input  [3:0] PCin,
  input  RESET,
  output Fetch,
  output wAD,
  output Write,
  output Source_Sel,
  output [1:0] RWrite_Sel,
  output [3:0] RX_Sel,
  output [3:0] RY_Sel,
  output [2:0] ALU_Sel,
  output [3:0] mAD,
  output [3:0] PCout,
  output wPC
);

  wire [3:0] decsel_1_selcode, XSel_selcode, Ysel_selcode;
  wire [11:0] ri_1_ri_out;

  RI ri_1 (.RI_In(In_in), .RI_Out({ri_1_ri_out[11:8], RWrite_Sel, mAD, ri_1_ri_out[1:0]}));
  PC_Increase pc_increase_1 (.in(PCin), .RESET(RESET), .out(PCout));
  DecSel XSel (.In(mAD[3:2]), .SelCode(XSel_selcode));
  DecSel Ysel (.In(mAD[1:0]), .SelCode(Ysel_selcode));
  RegW regw_1 (.OPCODE(ri_1_ri_out[11:8]), .Write(Write));
  SourceSel sourcesel_1 (.OPCODE(ri_1_ri_out[11:8]), .Write(Source_Sel));
  DecSel decsel_1 (.In(RWrite_Sel), .SelCode(decsel_1_selcode));
  ReadSelector readselector_1 (
    .X_in(XSel_selcode), .Y_in(Ysel_selcode), .X_out(RX_Sel), .Y_out(RY_Sel), .OPCODE(ri_1_ri_out[11:8]),
    .RegDest(decsel_1_selcode));
  Clock CLK (.out(wPC));
  WriteAD writead_1 (.OPCODE(ri_1_ri_out[11:8]), .wAD(wAD));
  ALU_Function alu_function_1 (.OPCODE(ri_1_ri_out[11:8]), .ALUCODE(ALU_Sel));

  assign Fetch = 1'b1;

  // Notes on the sheet:
  //   OPCODE
  //   REG_Dest
endmodule

// F_ALU
module ALU_Function (
  input  [3:0] OPCODE,
  output [2:0] ALUCODE
);

  wire not_1_out, not_2_out, not_3_out, not_4_out, not_5_out, not_6_out;

  not not_1 (not_1_out, OPCODE[2]);
  not not_2 (not_2_out, OPCODE[3]);
  not not_3 (not_3_out, OPCODE[2]);
  not not_4 (not_4_out, OPCODE[3]);
  not not_5 (not_5_out, OPCODE[1]);
  not not_6 (not_6_out, OPCODE[3]);
  and and_1 (ALUCODE[0], OPCODE[0], not_1_out, not_2_out);
  and and_2 (ALUCODE[1], OPCODE[1], not_3_out, not_4_out);
  and and_3 (ALUCODE[2], OPCODE[0], not_5_out, OPCODE[2], not_6_out);
endmodule

// S_Sel
module SourceSel (
  input  [3:0] OPCODE,
  output Write
);

  wire not_1_out, not_2_out, not_3_out;

  not not_1 (not_1_out, OPCODE[0]);
  not not_2 (not_2_out, OPCODE[1]);
  not not_3 (not_3_out, OPCODE[3]);
  and and_1 (Write, not_1_out, not_2_out, OPCODE[2], not_3_out);
endmodule

// wAD_F
module WriteAD (
  input  [3:0] OPCODE,
  output wAD
);

  wire not_1_out, not_2_out, not_3_out;

  not not_1 (not_1_out, OPCODE[0]);
  not not_2 (not_2_out, OPCODE[1]);
  not not_3 (not_3_out, OPCODE[2]);
  and and_1 (wAD, not_1_out, not_2_out, not_3_out, OPCODE[3]);
endmodule

module Imm_Format (
  input  [3:0] OPCODE,
  output wAD
);

  wire and_1_out, and_2_out, not_1_out, not_2_out, not_3_out, not_4_out, not_5_out, not_6_out;

  not not_1 (not_1_out, OPCODE[0]);
  not not_2 (not_2_out, OPCODE[1]);
  not not_3 (not_3_out, OPCODE[3]);
  not not_4 (not_4_out, OPCODE[0]);
  not not_5 (not_5_out, OPCODE[1]);
  not not_6 (not_6_out, OPCODE[2]);
  and and_1 (and_1_out, not_1_out, not_2_out, OPCODE[2], not_3_out);
  and and_2 (and_2_out, not_4_out, not_5_out, not_6_out, OPCODE[3]);
  or or_1 (wAD, and_1_out, and_2_out);
endmodule

module PC_Increase (
  input  [3:0] in,
  input  RESET,
  output [3:0] out
);

  wire full_adder_1_bit_1_c_o, full_adder_1_bit_2_c_o, half_adder_1_out_4, not_1_out;
  wire [3:0] half_adder_1_s;

  HALF_ADDER half_adder_1 (.A(in[0]), .B(1'b1), .out_4(half_adder_1_out_4), .S(half_adder_1_s[0]));
  FULL_ADDER_1_Bit full_adder_1_bit_1 (
    .A(in[1]), .B(1'b0), .C_i(half_adder_1_out_4), .S(half_adder_1_s[1]), .C_o(full_adder_1_bit_1_c_o));
  FULL_ADDER_1_Bit full_adder_1_bit_2 (
    .A(in[2]), .B(1'b0), .C_i(full_adder_1_bit_1_c_o), .S(half_adder_1_s[2]), .C_o(full_adder_1_bit_2_c_o));
  FULL_ADDER_1_Bit full_adder_1_bit_3 (
    .A(in[3]), .B(1'b0), .C_i(full_adder_1_bit_2_c_o), .S(half_adder_1_s[3]));  // open: C_o
  Multiplexer #(.width(4), .enable("false")) multiplexer_1 (
    .in0(4'b0000), .in1(half_adder_1_s), .out(out), .sel(not_1_out));
  not not_1 (not_1_out, RESET);
endmodule

module RegW (
  input  [3:0] OPCODE,
  output Write
);

  wire and_1_out, not_1_out, not_2_out, not_3_out;

  not not_1 (not_1_out, OPCODE[0]);
  not not_2 (not_2_out, OPCODE[1]);
  not not_3 (not_3_out, OPCODE[2]);
  and and_1 (and_1_out, not_1_out, not_2_out, not_3_out, OPCODE[3]);
  not not_4 (Write, and_1_out);
endmodule

module DecSel (
  input  [1:0] In,
  output [3:0] SelCode
);

  DEC_1_4 dec_1_4_1 (.in_1(In), .out_2(SelCode[0]), .out_3(SelCode[1]), .out_4(SelCode[2]), .out_5(SelCode[3]));
endmodule

// ReadSel
module ReadSelector (
  input  [3:0] RegDest,
  input  [3:0] X_in,
  input  [3:0] Y_in,
  input  [3:0] OPCODE,
  output [3:0] X_out,
  output [3:0] Y_out
);

  wire and_1_out, and_2_out, not_1_out, not_2_out, not_3_out, not_4_out, not_5_out, not_6_out, not_7_out,
       not_8_out, not_9_out, not_10_out, not_11_out, xnor_1_out;
  wire [3:0] buffer_1_out, controlled_buffer_1_out, controlled_buffer_3_out, controlled_buffer_5_out;

  assign controlled_buffer_1_out = not_1_out ? X_in : 4'bz;  // Controlled_Buffer controlled_buffer_1
  not not_1 (not_1_out, and_1_out);
  not not_2 (not_2_out, OPCODE[2]);
  assign controlled_buffer_1_out = and_1_out ? RegDest : 4'bz;  // Controlled_Buffer controlled_buffer_2
  and and_1 (and_1_out, OPCODE[3], not_2_out, not_3_out, not_4_out);
  not not_3 (not_3_out, OPCODE[1]);
  not not_4 (not_4_out, OPCODE[0]);
  assign buffer_1_out = controlled_buffer_1_out;  // Buffer buffer_1, 4 bits wide
  not not_5 (not_5_out, OPCODE[3]);
  assign controlled_buffer_3_out = and_2_out ? 4'b0000 : 4'bz;  // Controlled_Buffer controlled_buffer_3
  assign controlled_buffer_3_out = not_6_out ? buffer_1_out : 4'bz;  // Controlled_Buffer controlled_buffer_4
  not not_6 (not_6_out, and_2_out);
  and and_2 (and_2_out, not_5_out, OPCODE[2], not_7_out, not_8_out);
  not not_7 (not_7_out, OPCODE[1]);
  not not_8 (not_8_out, OPCODE[0]);
  assign controlled_buffer_5_out = xnor_1_out ? Y_in : 4'bz;  // Controlled_Buffer controlled_buffer_5
  assign controlled_buffer_5_out = not_9_out ? 4'b0000 : 4'bz;  // Controlled_Buffer controlled_buffer_6
  not not_9 (not_9_out, xnor_1_out);
  xnor xnor_1 (xnor_1_out, not_10_out, not_11_out);
  not not_10 (not_10_out, and_2_out);
  not not_11 (not_11_out, and_1_out);
  assign X_out = controlled_buffer_3_out;  // Buffer buffer_2, 4 bits wide
  assign Y_out = controlled_buffer_5_out;  // Buffer buffer_3, 4 bits wide
endmodule

module RI (
  input  [11:0] RI_In,
  output [11:0] RI_Out
);

  REGISTER_4_bits register_4_bits_1 (.READ(1'b1), .D(RI_In[3:0]), .out_4(RI_Out[3:0]), .Write(1'b1));
  REGISTER_4_bits register_4_bits_2 (.READ(1'b1), .D(RI_In[7:4]), .out_4(RI_Out[7:4]), .Write(1'b1));
  REGISTER_4_bits register_4_bits_3 (.READ(1'b1), .D(RI_In[11:8]), .out_4(RI_Out[11:8]), .Write(1'b1));
endmodule
