// Logisim project Projet.circ as structural Verilog
module HALF_ADDER (
  input  A,
  input  B,
  output S,
  output out_4
);

  and and_1 (out_4, A, B);
  xor xor_1 (S, A, B);
endmodule

module MUX_2___1 (
  input  A,
  input  B,
  input  SEL,
  output S
);

  wire and_1_out, and_2_out, not_1_out;

  not not_1 (not_1_out, SEL);
  buf and_1 (and_1_out, B);  // AND_Gate
  and and_2 (and_2_out, A, not_1_out);
  or or_1 (S, and_1_out, and_2_out);
endmodule

module FULL_ADDER_1_Bit (
  input  A,
  input  B,
  input  C_i,
  output S,
  output C_o
);

  wire and_1_out, and_2_out, xor_1_out;

  xor xor_1 (xor_1_out, A, B);
  and and_1 (and_1_out, A, B);
  and and_2 (and_2_out, xor_1_out, C_i);
  xor xor_2 (S, xor_1_out, C_i);
  or or_1 (C_o, and_1_out, and_2_out);
endmodule

module DEC_3_Bit (
  input  A0,
  input  A1,
  input  A2,
  output S0,
  output S1,
  output S2,
  output S3,
  output S4,
  output S5,
  output S6,
  output S7
);

  wire not_1_out, not_2_out, not_3_out, not_4_out, not_5_out, not_6_out, not_7_out, not_8_out, not_9_out,
       not_10_out, not_11_out, not_12_out;

  not not_1 (not_1_out, A0);
  not not_2 (not_2_out, A1);
  not not_3 (not_3_out, A2);
  not not_4 (not_4_out, A1);
  not not_5 (not_5_out, A2);
  not not_6 (not_6_out, A0);
  not not_7 (not_7_out, A2);
  not not_8 (not_8_out, A2);
  not not_9 (not_9_out, A0);
  not not_10 (not_10_out, A1);
  not not_11 (not_11_out, A1);
  not not_12 (not_12_out, A0);
  nand nand_1 (S0, not_1_out, not_2_out, not_3_out);
  nand nand_2 (S1, A0, not_4_out, not_5_out);
  nand nand_3 (S2, not_6_out, A1, not_7_out);
  nand nand_4 (S3, A0, A1, not_8_out);
  nand nand_5 (S4, not_9_out, not_10_out, A2);
  nand nand_6 (S5, A0, not_11_out, A2);
  nand nand_7 (S6, not_12_out, A1, A2);
  nand nand_8 (S7, A0, A1, A2);
endmodule

// ALU 1Bit
module ALU_1_bit (
  input  A,
  input  B,
  input  C_i,
  input  [2:0] in_4,
  output C_o,
  output out_6
);

  wire and_1_out, full_adder_1_bit_1_s, nand_1_out, nor_1_out, not_1_out, or_1_out, xnor_1_out, xor_1_out;

  FULL_ADDER_1_Bit full_adder_1_bit_1 (.A(A), .B(B), .C_i(C_i), .S(full_adder_1_bit_1_s), .C_o(C_o));
  not not_1 (not_1_out, B);
  xor xor_1 (xor_1_out, A, B);
  nor nor_1 (nor_1_out, A, B);
  and and_1 (and_1_out, A, B);
  or or_1 (or_1_out, A, B);
  nand nand_1 (nand_1_out, A, B);
  xnor xnor_1 (xnor_1_out, A, B);
  MUX_8__1 mux_8_1_1 (
    .in_1(xor_1_out), .in_2(nor_1_out), .in_3(full_adder_1_bit_1_s), .in_4(and_1_out), .in_5(or_1_out),
    .in_6(not_1_out), .in_7(nand_1_out), .in_8(xnor_1_out), .out_10(out_6), .in_9(in_4));
endmodule

// ALU
module ALU_PROC (
  input  [3:0] in_1,
  input  [3:0] in_2,
  input  Ci,
  input  [2:0] S,
  output Co,
  output [3:0] out_6
);

  wire alu_1_bit_1_c_o, alu_1_bit_2_c_o, alu_1_bit_3_c_o;

  ALU_1_bit alu_1_bit_1 (.C_i(Ci), .A(in_1[0]), .B(in_2[0]), .C_o(alu_1_bit_1_c_o), .out_6(out_6[0]), .in_4(S));
  ALU_1_bit alu_1_bit_2 (
    .C_i(alu_1_bit_1_c_o), .A(in_1[1]), .B(in_2[1]), .C_o(alu_1_bit_2_c_o), .out_6(out_6[1]), .in_4(S));
  ALU_1_bit alu_1_bit_3 (
    .C_i(alu_1_bit_2_c_o), .A(in_1[2]), .B(in_2[2]), .C_o(alu_1_bit_3_c_o), .out_6(out_6[2]), .in_4(S));
  ALU_1_bit alu_1_bit_4 (.C_i(alu_1_bit_3_c_o), .A(in_1[3]), .B(in_2[3]), .C_o(Co), .out_6(out_6[3]), .in_4(S));
endmodule

module PROC (
);

  wire alu_proc_1_co, undriven;
  wire [2:0] undriven_2;
  wire [3:0] alu_proc_1_out_6, undriven_3, undriven_4;

  ALU_PROC alu_proc_1 (
    .Ci(undriven), .Co(alu_proc_1_co), .S(undriven_2), .in_1(undriven_3), .in_2(undriven_4),
    .out_6(alu_proc_1_out_6));
endmodule

// MUX
module MUX_8__1 (
  input  in_1,
  input  in_2,
  input  in_3,
  input  in_4,
  input  in_5,
  input  in_6,
  input  in_7,
  input  in_8,
  input  [2:0] in_9,
  output out_10
);

  wire and_1_out, and_2_out, and_3_out, and_4_out, and_5_out, and_6_out, and_7_out, and_8_out, not_1_out,
       not_2_out, not_3_out;

  not not_1 (not_1_out, in_9[2]);
  not not_2 (not_2_out, in_9[1]);
  not not_3 (not_3_out, in_9[0]);
  and and_1 (and_1_out, in_1, not_1_out, not_2_out, not_3_out);
  and and_2 (and_2_out, in_2, not_1_out, not_2_out, in_9[0]);
  and and_3 (and_3_out, in_3, not_1_out, in_9[1], not_3_out);
  and and_4 (and_4_out, in_4, not_1_out, in_9[1], in_9[0]);
  and and_5 (and_5_out, in_5, in_9[2], not_2_out, not_3_out);
  and and_6 (and_6_out, in_6, in_9[2], not_2_out, in_9[0]);
  and and_7 (and_7_out, in_7, in_9[2], in_9[1], not_3_out);
  and and_8 (and_8_out, in_8, in_9[2], in_9[1], in_9[0]);
  or or_1 (out_10, and_1_out, and_2_out, and_3_out, and_4_out, and_5_out, and_6_out, and_7_out, and_8_out);
endmodule

// MUX 4BIT
module MUX_8__1_4BIT (
  input  [3:0] in_1,
  input  [3:0] in_2,
  input  [3:0] in_3,
  input  [3:0] in_4,
  input  [3:0] in_5,
  input  [3:0] in_6,
  input  [3:0] in_7,
  input  [3:0] in_8,
  input  [2:0] in_9,
  output [3:0] out_10
);

  MUX_8__1 mux_8_1_1 (
    .in_1(in_1[0]), .in_2(in_2[0]), .in_3(in_3[0]), .in_4(in_4[0]), .in_5(in_5[0]), .in_6(in_6[0]),
    .in_7(in_7[0]), .in_8(in_8[0]), .out_10(out_10[0]), .in_9(in_9));
  MUX_8__1 mux_8_1_2 (
    .in_1(in_1[1]), .in_2(in_2[1]), .in_3(in_3[1]), .in_4(in_4[1]), .in_5(in_5[1]), .in_6(in_6[1]),
    .in_7(in_7[1]), .in_8(in_8[1]), .out_10(out_10[1]), .in_9(in_9));
  MUX_8__1 mux_8_1_3 (
    .in_1(in_1[2]), .in_2(in_2[2]), .in_3(in_3[2]), .in_4(in_4[2]), .in_5(in_5[2]), .in_6(in_6[2]),
    .in_7(in_7[2]), .in_8(in_8[2]), .out_10(out_10[2]), .in_9(in_9));
  MUX_8__1 mux_8_1_4 (
    .in_1(in_1[3]), .in_2(in_2[3]), .in_3(in_3[3]), .in_4(in_4[3]), .in_5(in_5[3]), .in_6(in_6[3]),
    .in_7(in_7[3]), .in_8(in_8[3]), .out_10(out_10[3]), .in_9(in_9));
endmodule
