// Logisim project REGISTER.circ as structural Verilog: 5 circuits, main circuit main
module main (
  input  [3:0] Din,
  input  [2:0] R,
  input  Read,
  input  Write,
  input  [2:0] Rx,
  input  [2:0] Ry,
  input  [2:0] in_7,
  input  [3:0] in_8,
  input  in_9,
  input  in_10,
  input  in_11,
  output [3:0] out_12,
  output [3:0] out_13
);

  RegFile_8Reg regfile_8reg_1 (
    .RegNbr(R), .Sx(out_12), .Sy(out_13), .Write(Write), .Read(Read), .Din(Din), .Ry(Ry), .Rx(Rx));
  RAM #(.addrWidth(3), .dataWidth(4)) ram_1 (
    .addr(in_7), .data(in_8), .sel(in_9), .clk(in_10), .ld(in_11));  // open: clr
endmodule

// REGISTER
module REGISTER_4_bits (
  input  [3:0] D,
  input  Write,
  input  READ,
  output [3:0] out_4
);

  wire CLK_out, controlled_buffer_1_out, controlled_buffer_2_out, controlled_buffer_3_out,
       controlled_buffer_4_out, register_1_q, register_2_q, register_3_q, register_4_q;

  Clock CLK (.out(CLK_out));
  assign controlled_buffer_1_out = Write ? D[3] : 1'bz;  // Controlled_Buffer controlled_buffer_1
  Register #(.width(1)) register_1 (.D(controlled_buffer_1_out), .Q(register_1_q), .clk(CLK_out));  // open: en, clr
  and and_1 (out_4[3], READ, register_1_q);
  assign controlled_buffer_2_out = Write ? D[2] : 1'bz;  // Controlled_Buffer controlled_buffer_2
  Register #(.width(1)) register_2 (.D(controlled_buffer_2_out), .Q(register_2_q), .clk(CLK_out));  // open: en, clr
  and and_2 (out_4[2], READ, register_2_q);
  assign controlled_buffer_3_out = Write ? D[1] : 1'bz;  // Controlled_Buffer controlled_buffer_3
  Register #(.width(1)) register_3 (.D(controlled_buffer_3_out), .Q(register_3_q), .clk(CLK_out));  // open: en, clr
  and and_3 (out_4[1], READ, register_3_q);
  assign controlled_buffer_4_out = Write ? D[0] : 1'bz;  // Controlled_Buffer controlled_buffer_4
  Register #(.width(1)) register_4 (.D(controlled_buffer_4_out), .Q(register_4_q), .clk(CLK_out));  // open: en, clr
  and and_4 (out_4[0], READ, register_4_q);
endmodule

// RegFile
module RegFile_8Reg (
  input  Write,
  input  Read,
  input  [3:0] Din,
  input  [2:0] RegNbr,
  input  [2:0] Ry,
  input  [2:0] Rx,
  output [3:0] Sx,
  output [3:0] Sy
);

  wire and_1_out, and_2_out, and_3_out, and_4_out, and_5_out, and_6_out, and_7_out, and_8_out,
       dec_3bit_1_out_2, dec_3bit_1_out_3, dec_3bit_1_out_4, dec_3bit_1_out_5, dec_3bit_1_out_6,
       dec_3bit_1_out_7, dec_3bit_1_out_8, dec_3bit_1_out_9;
  wire [3:0] register_4_bits_1_out_4, register_4_bits_2_out_4, register_4_bits_3_out_4,
       register_4_bits_4_out_4, register_4_bits_5_out_4, register_4_bits_6_out_4, register_4_bits_7_out_4,
       register_4_bits_8_out_4;

  DEC_3Bit dec_3bit_1 (
    .in_1(RegNbr), .out_2(dec_3bit_1_out_2), .out_3(dec_3bit_1_out_3), .out_4(dec_3bit_1_out_4),
    .out_5(dec_3bit_1_out_5), .out_6(dec_3bit_1_out_6), .out_7(dec_3bit_1_out_7), .out_8(dec_3bit_1_out_8),
    .out_9(dec_3bit_1_out_9));
  and and_1 (and_1_out, Write, dec_3bit_1_out_2);
  and and_2 (and_2_out, Write, dec_3bit_1_out_3);
  and and_3 (and_3_out, Write, dec_3bit_1_out_4);
  and and_4 (and_4_out, Write, dec_3bit_1_out_5);
  and and_5 (and_5_out, Write, dec_3bit_1_out_6);
  and and_6 (and_6_out, Write, dec_3bit_1_out_7);
  and and_7 (and_7_out, Write, dec_3bit_1_out_8);
  and and_8 (and_8_out, dec_3bit_1_out_9, Write);
  REGISTER_4_bits register_4_bits_1 (.READ(Read), .D(Din), .out_4(register_4_bits_1_out_4), .Write(and_1_out));
  REGISTER_4_bits register_4_bits_2 (.READ(Read), .D(Din), .out_4(register_4_bits_2_out_4), .Write(and_2_out));
  REGISTER_4_bits register_4_bits_3 (.READ(Read), .D(Din), .out_4(register_4_bits_3_out_4), .Write(and_3_out));
  REGISTER_4_bits register_4_bits_4 (.READ(Read), .D(Din), .out_4(register_4_bits_4_out_4), .Write(and_4_out));
  REGISTER_4_bits register_4_bits_5 (.READ(Read), .D(Din), .out_4(register_4_bits_5_out_4), .Write(and_5_out));
  REGISTER_4_bits register_4_bits_6 (.READ(Read), .D(Din), .out_4(register_4_bits_6_out_4), .Write(and_6_out));
  REGISTER_4_bits register_4_bits_7 (.READ(Read), .D(Din), .out_4(register_4_bits_7_out_4), .Write(and_7_out));
  REGISTER_4_bits register_4_bits_8 (.READ(Read), .D(Din), .out_4(register_4_bits_8_out_4), .Write(and_8_out));
  MUX_8__1_4_Bit mux_8_1_4_bit_1 (
    .in_9(Rx), .out_10(Sx), .in_1(register_4_bits_1_out_4), .in_2(register_4_bits_2_out_4),
    .in_3(register_4_bits_3_out_4), .in_4(register_4_bits_4_out_4), .in_5(register_4_bits_5_out_4),
    .in_6(register_4_bits_6_out_4), .in_7(register_4_bits_7_out_4), .in_8(register_4_bits_8_out_4));
  MUX_8__1_4_Bit mux_8_1_4_bit_2 (
    .in_9(Ry), .out_10(Sy), .in_1(register_4_bits_1_out_4), .in_2(register_4_bits_2_out_4),
    .in_3(register_4_bits_3_out_4), .in_4(register_4_bits_4_out_4), .in_5(register_4_bits_5_out_4),
    .in_6(register_4_bits_6_out_4), .in_7(register_4_bits_7_out_4), .in_8(register_4_bits_8_out_4));
endmodule

module RegFile (
  input  Write,
  input  [3:0] Din,
  input  [3:0] Xsel,
  input  [1:0] RegSel,
  input  [3:0] Ysel,
  output [3:0] XOut,
  output [3:0] YOut
);

  wire and_1_out, and_2_out, and_3_out, and_4_out, dec_1_4_1_out_2, dec_1_4_1_out_3, dec_1_4_1_out_4,
       dec_1_4_1_out_5;
  wire [3:0] register_4_bits_1_out_4, register_4_bits_2_out_4, register_4_bits_3_out_4,
       register_4_bits_4_out_4;

  DEC_1_4 dec_1_4_1 (
    .in_1(RegSel), .out_2(dec_1_4_1_out_2), .out_3(dec_1_4_1_out_3), .out_4(dec_1_4_1_out_4),
    .out_5(dec_1_4_1_out_5));
  and and_1 (and_1_out, Write, dec_1_4_1_out_2);
  and and_2 (and_2_out, Write, dec_1_4_1_out_3);
  and and_3 (and_3_out, Write, dec_1_4_1_out_4);
  and and_4 (and_4_out, Write, dec_1_4_1_out_5);
  REGISTER_4_bits register_4_bits_1 (.READ(1'b1), .D(Din), .out_4(register_4_bits_1_out_4), .Write(and_1_out));
  REGISTER_4_bits register_4_bits_2 (.READ(1'b1), .D(Din), .out_4(register_4_bits_2_out_4), .Write(and_2_out));
  REGISTER_4_bits register_4_bits_3 (.READ(1'b1), .D(Din), .out_4(register_4_bits_3_out_4), .Write(and_3_out));
  REGISTER_4_bits register_4_bits_4 (.READ(1'b1), .D(Din), .out_4(register_4_bits_4_out_4), .Write(and_4_out));
  RegSel regsel_1 (
    .in_1(register_4_bits_1_out_4), .in_2(register_4_bits_2_out_4), .in_3(register_4_bits_3_out_4),
    .in_4(register_4_bits_4_out_4), .out_9(XOut), ._3(Xsel[3]), ._2(Xsel[2]), ._1(Xsel[1]), ._0(Xsel[0]));
  RegSel regsel_2 (
    .in_1(register_4_bits_1_out_4), .in_2(register_4_bits_2_out_4), .in_3(register_4_bits_3_out_4),
    .in_4(register_4_bits_4_out_4), .out_9(YOut), ._3(Ysel[3]), ._2(Ysel[2]), ._1(Ysel[1]), ._0(Ysel[0]));
endmodule

module RegSel (
  input  [3:0] in_1,
  input  [3:0] in_2,
  input  [3:0] in_3,
  input  [3:0] in_4,
  input  _3,
  input  _2,
  input  _1,
  input  _0,
  output [3:0] out_9
);

  wire nor_1_out;
  wire [3:0] controlled_buffer_1_out;

  assign controlled_buffer_1_out = _3 ? in_4 : 4'bz;  // Controlled_Buffer controlled_buffer_1
  assign controlled_buffer_1_out = _1 ? in_2 : 4'bz;  // Controlled_Buffer controlled_buffer_2
  assign controlled_buffer_1_out = _2 ? in_3 : 4'bz;  // Controlled_Buffer controlled_buffer_3
  assign controlled_buffer_1_out = _0 ? in_1 : 4'bz;  // Controlled_Buffer controlled_buffer_4
  assign controlled_buffer_1_out = nor_1_out ? 4'b0000 : 4'bz;  // Controlled_Buffer controlled_buffer_5
  nor nor_1 (nor_1_out, _0, _1, _2, _3);
  assign out_9 = controlled_buffer_1_out;  // Buffer buffer_1, 4 bits wide
endmodule
