// Logisim project lib.circ as structural Verilog: 15 circuits, main circuit main
module main (
  input  [3:0] in_1,
  input  [3:0] in_2,
  input  [2:0] in_3,
  output [3:0] out_4
);

  // MUX_8__1_4_Bit mux_8_1_4_bit_1: pin names not known; wires that end beside it: in_1, in_2, in_3, out_4
endmodule

module HALF_ADDER (
  input  A,
  input  B,
  output S,
  output out_4
);

  and and_1 (out_4, A, B);
  xor xor_1 (S, A, B);
endmodule

module MUX_2__1 (
  input  A,
  input  B,
  input  SEL,
  output S
);

  wire and_1_out, and_2_out, not_1_out;

  not not_1 (not_1_out, SEL);
  and and_1 (and_1_out, B, SEL);
  and and_2 (and_2_out, A, not_1_out);
  or or_1 (S, and_1_out, and_2_out);
endmodule

module FULL_ADDER_1_Bit (
  input  A,
  input  B,
  input  C_i,
  output S,
  output C_o
);

  wire and_1_out, and_2_out, xor_1_out;

  xor xor_1 (xor_1_out, A, B);
  and and_1 (and_1_out, A, B);
  and and_2 (and_2_out, xor_1_out, C_i);
  xor xor_2 (S, xor_1_out, C_i);
  or or_1 (C_o, and_1_out, and_2_out);
endmodule

// DEC
module DEC_3Bit (
  input  [2:0] in_1,
  output out_2,
  output out_3,
  output out_4,
  output out_5,
  output out_6,
  output out_7,
  output out_8,
  output out_9
);

  wire not_1_out, not_2_out, not_3_out;

  not not_1 (not_1_out, in_1[2]);
  not not_2 (not_2_out, in_1[1]);
  not not_3 (not_3_out, in_1[0]);
  and and_1 (out_2, not_1_out, not_2_out, not_3_out);
  and and_2 (out_3, not_1_out, not_2_out, in_1[0]);
  and and_3 (out_4, not_1_out, in_1[1], not_3_out);
  and and_4 (out_5, not_1_out, in_1[1], in_1[0]);
  and and_5 (out_6, in_1[2], not_2_out, not_3_out);
  and and_6 (out_7, in_1[2], not_2_out, in_1[0]);
  and and_7 (out_8, in_1[2], in_1[1], not_3_out);
  and and_8 (out_9, in_1[2], in_1[1], in_1[0]);
endmodule

// MUX
module MUX_8__1_1Bit (
  input  in_1,
  input  in_2,
  input  in_3,
  input  in_4,
  input  in_5,
  input  in_6,
  input  in_7,
  input  in_8,
  input  [2:0] in_9,
  output out_10
);

  wire and_1_out, and_2_out, and_3_out, and_4_out, and_5_out, and_6_out, and_7_out, and_8_out, not_1_out,
       not_2_out, not_3_out;

  not not_1 (not_1_out, in_9[2]);
  not not_2 (not_2_out, in_9[1]);
  not not_3 (not_3_out, in_9[0]);
  and and_1 (and_1_out, in_1, not_1_out, not_2_out, not_3_out);
  and and_2 (and_2_out, in_2, not_1_out, not_2_out, in_9[0]);
  and and_3 (and_3_out, in_3, not_1_out, in_9[1], not_3_out);
  and and_4 (and_4_out, in_4, not_1_out, in_9[1], in_9[0]);
  and and_5 (and_5_out, in_5, in_9[2], not_2_out, not_3_out);
  and and_6 (and_6_out, in_6, in_9[2], not_2_out, in_9[0]);
  and and_7 (and_7_out, in_7, in_9[2], in_9[1], not_3_out);
  and and_8 (and_8_out, in_8, in_9[2], in_9[1], in_9[0]);
  or or_1 (out_10, and_1_out, and_2_out, and_3_out, and_4_out, and_5_out, and_6_out, and_7_out, and_8_out);
endmodule

// D Latch
module DLatch (
  input  D,
  input  CLK,
  output S_B,
  output S
);

  wire and_1_out, and_2_out, not_1_out;

  not not_1 (not_1_out, D);
  and and_1 (and_1_out, D, CLK);
  and and_2 (and_2_out, not_1_out, CLK);
  nor nor_1 (S_B, and_1_out, S);
  nor nor_2 (S, S_B, and_2_out);
endmodule

module MAJ (
  input  a,
  input  b,
  input  c,
  output out_4
);

  wire and_1_out, and_2_out, and_3_out, and_4_out, not_1_out, not_2_out, not_3_out;

  not not_1 (not_1_out, a);
  not not_2 (not_2_out, b);
  not not_3 (not_3_out, c);
  and and_1 (and_1_out, not_1_out, b, c);
  and and_2 (and_2_out, a, not_2_out, c);
  and and_3 (and_3_out, a, b, not_3_out);
  and and_4 (and_4_out, c, b, a);
  or or_1 (out_4, and_1_out, and_2_out, and_3_out, and_4_out);
endmodule

// COMP
module COMP_4Bit (
  input  [3:0] a,
  input  [3:0] b,
  output out_3
);

  wire xor_1_out, xor_2_out, xor_3_out, xor_4_out;

  xor xor_1 (xor_1_out, a[0], b[0]);
  xor xor_2 (xor_2_out, a[1], b[1]);
  xor xor_3 (xor_3_out, a[2], b[2]);
  xor xor_4 (xor_4_out, a[3], b[3]);
  nor nor_1 (out_3, xor_1_out, xor_2_out, xor_3_out, xor_4_out);
endmodule

// Decal_4B
module Decal_4Bit (
  input  [3:0] D,
  input  C,
  output [3:0] out_3
);

  wire and_1_out, and_3_out, and_4_out, and_6_out, not_1_out;

  not not_1 (not_1_out, C);
  and and_1 (and_1_out, D[0], C);
  and and_2 (out_3[0], not_1_out, D[1]);
  or or_1 (out_3[1], and_1_out, and_4_out);
  and and_3 (and_3_out, D[1], C);
  and and_4 (and_4_out, not_1_out, D[2]);
  or or_2 (out_3[2], and_3_out, and_6_out);
  and and_5 (out_3[3], D[2], C);
  and and_6 (and_6_out, not_1_out, D[3]);
endmodule

module D_Flip_Flop (
  input  D,
  input  CLK,
  output S_B,
  output S
);

  wire and_1_out, and_2_out, and_3_out, not_1_out, not_2_out;

  not not_1 (not_1_out, D);
  not not_2 (not_2_out, CLK);
  and and_1 (and_1_out, CLK, not_2_out);
  and and_2 (and_2_out, D, and_1_out);
  and and_3 (and_3_out, and_1_out, not_1_out);
  nor nor_1 (S_B, and_2_out, S);
  nor nor_2 (S, S_B, and_3_out);
endmodule

// MUX 4Bit
module MUX_8__1_4_Bit (
  input  [3:0] in_1,
  input  [3:0] in_2,
  input  [3:0] in_3,
  input  [3:0] in_4,
  input  [3:0] in_5,
  input  [3:0] in_6,
  input  [3:0] in_7,
  input  [3:0] in_8,
  input  [2:0] in_9,
  output [3:0] out_10
);

  MUX_8__1_1Bit mux_8_1_1bit_1 (
    .in_1(in_1[0]), .in_2(in_2[0]), .in_3(in_3[0]), .in_4(in_4[0]), .in_5(in_5[0]), .in_6(in_6[0]),
    .in_7(in_7[0]), .in_8(in_8[0]), .out_10(out_10[0]), .in_9(in_9));
  MUX_8__1_1Bit mux_8_1_1bit_2 (
    .in_1(in_1[1]), .in_2(in_2[1]), .in_3(in_3[1]), .in_4(in_4[1]), .in_5(in_5[1]), .in_6(in_6[1]),
    .in_7(in_7[1]), .in_8(in_8[1]), .out_10(out_10[1]), .in_9(in_9));
  MUX_8__1_1Bit mux_8_1_1bit_3 (
    .in_1(in_1[2]), .in_2(in_2[2]), .in_3(in_3[2]), .in_4(in_4[2]), .in_5(in_5[2]), .in_6(in_6[2]),
    .in_7(in_7[2]), .in_8(in_8[2]), .out_10(out_10[2]), .in_9(in_9));
  MUX_8__1_1Bit mux_8_1_1bit_4 (
    .in_1(in_1[3]), .in_2(in_2[3]), .in_3(in_3[3]), .in_4(in_4[3]), .in_5(in_5[3]), .in_6(in_6[3]),
    .in_7(in_7[3]), .in_8(in_8[3]), .out_10(out_10[3]), .in_9(in_9));
endmodule

// DEC 2Sbit
module DEC_1_4 (
  input  [1:0] in_1,
  output out_2,
  output out_3,
  output out_4,
  output out_5
);

  wire not_1_out, not_2_out;

  not not_1 (not_1_out, in_1[0]);
  not not_2 (not_2_out, in_1[1]);
  and and_1 (out_2, not_1_out, not_2_out);
  and and_2 (out_3, in_1[0], not_2_out);
  and and_3 (out_4, in_1[1], not_1_out);
  and and_4 (out_5, in_1[0], in_1[1]);
endmodule

// MUX 4_1
module MUX_4__1 (
  input  A,
  input  B,
  input  C,
  input  D,
  input  [1:0] Sel,
  output out_6
);

  wire mux_2_1_1_s, mux_2_1_2_s;

  MUX_2__1 mux_2_1_1 (.S(mux_2_1_1_s), .A(A), .B(B), .SEL(Sel[0]));
  MUX_2__1 mux_2_1_2 (.S(mux_2_1_2_s), .A(C), .B(D), .SEL(Sel[0]));
  MUX_2__1 mux_2_1_3 (.S(out_6), .A(mux_2_1_1_s), .B(mux_2_1_2_s), .SEL(Sel[1]));
endmodule

// MUX4_1 4B
module MUX_4__1_4Bit (
  input  [3:0] A,
  input  [3:0] B,
  input  [3:0] C,
  input  [3:0] D,
  input  [1:0] Sel,
  output [3:0] out_6
);

  MUX_4__1 X0 (.A(A[0]), .B(B[0]), .C(C[0]), .D(D[0]), .out_6(out_6[0]), .Sel(Sel));
  MUX_4__1 X1 (.A(A[1]), .B(B[1]), .C(C[1]), .D(D[1]), .out_6(out_6[1]), .Sel(Sel));
  MUX_4__1 X2 (.A(A[2]), .B(B[2]), .C(C[2]), .D(D[2]), .out_6(out_6[2]), .Sel(Sel));
  MUX_4__1 X3 (.A(A[3]), .B(B[3]), .C(C[3]), .D(D[3]), .out_6(out_6[3]), .Sel(Sel));
endmodule
